// Logisim project ALU.circ as structural Verilog: 1 circuit, main circuit ALU
module ALU (
  input  [31:0] A,
  input  [31:0] B,
  input  [4:0] Shift,
  input  [3:0] Codop,
  input  CarryIn,
  output [31:0] S,
  output [3:0] Flags
);

  wire bitselector_5_out, bitselector_6_out, bitselector_7_out, bitselector_8_out, bitselector_9_out,
       bitselector_10_out, bitselector_11_out, bitselector_12_out, bitselector_13_out, bitselector_14_out,
       bitselector_15_out, bitselector_16_out, bitselector_17_out, bitselector_18_out, bitselector_19_out,
       bitselector_20_out, comparator_1_eq, comparator_1_lt, CoutADC, CoutASR, CoutCMN, CoutCMP, CoutLSL,
       CoutLSR, CoutROR, CoutSBC, decoder_1_out0, decoder_1_out1, decoder_1_out2, decoder_1_out3,
       decoder_1_out4, decoder_1_out5, decoder_1_out6, decoder_1_out7, decoder_1_out8, decoder_1_out9,
       decoder_1_out10, decoder_1_out11, decoder_1_out12, decoder_1_out13, decoder_1_out14, decoder_1_out15,
       not_3_out, subtractor_1_bout, VADC, VCMN, VCMP, VRSD, VSBC, xnor_1_out, xnor_2_out, xor_2_out,
       xor_3_out, xor_4_out, xor_5_out, xor_6_out, xor_7_out;
  wire [4:0] subtractor_3_out, subtractor_4_out, subtractor_5_out;
  wire [31:0] adder_1_out, adder_2_out, and_1_out, and_2_out, and_3_out, multiplier_1_cout, multiplier_1_out,
       negator_1_out, not_1_out, not_2_out, or_1_out, R, shifter_1_out, shifter_2_out, shifter_3_out,
       shifter_4_out, subtractor_1_out, subtractor_2_out, xor_1_out;

  Decoder #(.select(4)) decoder_1 (
    .out0(decoder_1_out0), .out1(decoder_1_out1), .out2(decoder_1_out2), .out3(decoder_1_out3),
    .out4(decoder_1_out4), .out5(decoder_1_out5), .out6(decoder_1_out6), .out7(decoder_1_out7),
    .out8(decoder_1_out8), .out9(decoder_1_out9), .out10(decoder_1_out10), .out11(decoder_1_out11),
    .out12(decoder_1_out12), .out13(decoder_1_out13), .out14(decoder_1_out14), .out15(decoder_1_out15),
    .sel(Codop), .en(1'b1));
  assign not_1_out = ~A;  // NOT_Gate not_1, 32 bits wide
  assign not_2_out = ~A;  // NOT_Gate not_2, 32 bits wide
  assign and_1_out = A & B;  // AND_Gate and_1, 32 bits wide
  assign R = decoder_1_out0 ? and_1_out : 32'bz;  // Controlled_Buffer controlled_buffer_1
  assign xor_1_out = A ^ B;  // XOR_Gate xor_1, 32 bits wide
  Shifter #(.width(32)) shifter_1 (.in(B), .\dist (Shift), .out(shifter_1_out));
  Shifter #(.shift("lr"), .width(32)) shifter_2 (.in(B), .\dist (Shift), .out(shifter_2_out));
  Shifter #(.shift("ar"), .width(32)) shifter_3 (.in(B), .\dist (Shift), .out(shifter_3_out));
  Adder #(.width(32)) adder_1 (.a(A), .b(B), .out(adder_1_out), .cin(CarryIn), .cout(CoutADC));
  not not_3 (not_3_out, CarryIn);
  Subtractor #(.width(32)) subtractor_1 (
    .a(B), .b(A), .out(subtractor_1_out), .bin(not_3_out), .bout(subtractor_1_bout));
  Shifter #(.shift("rr"), .width(32)) shifter_4 (.in(B), .\dist (Shift), .out(shifter_4_out));
  assign and_2_out = A & B;  // AND_Gate and_2, 32 bits wide
  Negator #(.width(32)) negator_1 (.in(A), .out(negator_1_out));
  Subtractor #(.width(32)) subtractor_2 (.a(B), .b(A), .out(subtractor_2_out));  // open: bin, bout
  Adder #(.width(32)) adder_2 (.a(A), .b(B), .out(adder_2_out), .cout(CoutCMN));  // open: cin
  assign or_1_out = A | B;  // OR_Gate or_1, 32 bits wide
  Multiplier #(.width(32)) multiplier_1 (.a(A), .b(B), .out(multiplier_1_out), .cout(multiplier_1_cout));  // open: cin
  assign and_3_out = B & not_1_out;  // AND_Gate and_3, 32 bits wide
  assign R = decoder_1_out1 ? xor_1_out : 32'bz;  // Controlled_Buffer controlled_buffer_2
  assign R = decoder_1_out2 ? shifter_1_out : 32'bz;  // Controlled_Buffer controlled_buffer_3
  assign R = decoder_1_out3 ? shifter_2_out : 32'bz;  // Controlled_Buffer controlled_buffer_4
  assign R = decoder_1_out4 ? shifter_3_out : 32'bz;  // Controlled_Buffer controlled_buffer_5
  assign R = decoder_1_out5 ? adder_1_out : 32'bz;  // Controlled_Buffer controlled_buffer_6
  assign R = decoder_1_out6 ? subtractor_1_out : 32'bz;  // Controlled_Buffer controlled_buffer_7
  assign R = decoder_1_out7 ? shifter_4_out : 32'bz;  // Controlled_Buffer controlled_buffer_8
  assign R = decoder_1_out8 ? and_2_out : 32'bz;  // Controlled_Buffer controlled_buffer_9
  assign R = decoder_1_out9 ? negator_1_out : 32'bz;  // Controlled_Buffer controlled_buffer_10
  assign R = decoder_1_out10 ? subtractor_2_out : 32'bz;  // Controlled_Buffer controlled_buffer_11
  assign R = decoder_1_out11 ? adder_2_out : 32'bz;  // Controlled_Buffer controlled_buffer_12
  assign R = decoder_1_out12 ? or_1_out : 32'bz;  // Controlled_Buffer controlled_buffer_13
  assign R = decoder_1_out13 ? multiplier_1_out : 32'bz;  // Controlled_Buffer controlled_buffer_14
  assign R = decoder_1_out14 ? and_3_out : 32'bz;  // Controlled_Buffer controlled_buffer_15
  assign R = decoder_1_out15 ? not_2_out : 32'bz;  // Controlled_Buffer controlled_buffer_16
  BitSelector #(.width(32)) bitselector_1 (.in(A), .out(CoutLSL), .sel(subtractor_3_out));
  not not_4 (CoutSBC, subtractor_1_bout);
  BitSelector #(.width(32)) bitselector_2 (.in(R), .out(CoutROR), .sel({5{1'b1}}));
  Comparator #(.mode("unsigned"), .width(32)) comparator_1 (
    .a(A), .b(B), .eq(comparator_1_eq), .lt(comparator_1_lt));  // open: gt
  Subtractor #(.width(5)) subtractor_3 (.a({5{1'b0}}), .b(Shift), .out(subtractor_3_out));  // open: bin, bout
  BitSelector #(.width(32)) bitselector_3 (.in(B), .out(CoutLSR), .sel(subtractor_4_out));
  Subtractor #(.width(5)) subtractor_4 (.a(Shift), .b(5'b00001), .out(subtractor_4_out));  // open: bin, bout
  BitSelector #(.width(32)) bitselector_4 (.in(B), .out(CoutASR), .sel(subtractor_5_out));
  Subtractor #(.width(5)) subtractor_5 (.a(Shift), .b(5'b00001), .out(subtractor_5_out));  // open: bin, bout
  or or_2 (CoutCMP, comparator_1_lt, comparator_1_eq);
  BitSelector #(.width(32)) bitselector_5 (.in(R), .out(bitselector_5_out), .sel({5{1'b1}}));
  BitSelector #(.width(32)) bitselector_6 (.in(A), .out(bitselector_6_out), .sel({5{1'b1}}));
  BitSelector #(.width(32)) bitselector_7 (.in(A), .out(bitselector_7_out), .sel({5{1'b1}}));
  BitSelector #(.width(32)) bitselector_8 (.in(B), .out(bitselector_8_out), .sel({5{1'b1}}));
  BitSelector #(.width(32)) bitselector_9 (.in(R), .out(bitselector_9_out), .sel({5{1'b1}}));
  BitSelector #(.width(32)) bitselector_10 (.in(B), .out(bitselector_10_out), .sel({5{1'b1}}));
  BitSelector #(.width(32)) bitselector_11 (.in(A), .out(bitselector_11_out), .sel({5{1'b1}}));
  BitSelector #(.width(32)) bitselector_12 (.in(B), .out(bitselector_12_out), .sel({5{1'b1}}));
  BitSelector #(.width(32)) bitselector_13 (.in(R), .out(bitselector_13_out), .sel({5{1'b1}}));
  BitSelector #(.width(32)) bitselector_14 (.in(B), .out(bitselector_14_out), .sel({5{1'b1}}));
  BitSelector #(.width(32)) bitselector_15 (.in(A), .out(bitselector_15_out), .sel({5{1'b1}}));
  BitSelector #(.width(32)) bitselector_16 (.in(B), .out(bitselector_16_out), .sel({5{1'b1}}));
  BitSelector #(.width(32)) bitselector_17 (.in(R), .out(bitselector_17_out), .sel({5{1'b1}}));
  BitSelector #(.width(32)) bitselector_18 (.in(A), .out(bitselector_18_out), .sel({5{1'b1}}));
  BitSelector #(.width(32)) bitselector_19 (.in(A), .out(bitselector_19_out), .sel({5{1'b1}}));
  BitSelector #(.width(32)) bitselector_20 (.in(B), .out(bitselector_20_out), .sel({5{1'b1}}));
  xnor xnor_1 (xnor_1_out, bitselector_7_out, bitselector_8_out);
  xor xor_2 (xor_2_out, bitselector_11_out, bitselector_12_out);
  Comparator #(.width(32)) comparator_2 (.a(A), .b(32'h80000000), .eq(VRSD));  // open: gt, lt
  xor xor_3 (xor_3_out, bitselector_15_out, bitselector_16_out);
  xnor xnor_2 (xnor_2_out, bitselector_19_out, bitselector_20_out);
  xor xor_4 (xor_4_out, bitselector_5_out, bitselector_6_out);
  xor xor_5 (xor_5_out, bitselector_9_out, bitselector_10_out);
  xor xor_6 (xor_6_out, bitselector_13_out, bitselector_14_out);
  xor xor_7 (xor_7_out, bitselector_17_out, bitselector_18_out);
  and and_4 (VADC, xor_4_out, xnor_1_out);
  and and_5 (VSBC, xor_5_out, xor_2_out);
  and and_6 (VCMP, xor_6_out, xor_3_out);
  and and_7 (VCMN, xor_7_out, xnor_2_out);
  Comparator #(.width(32)) comparator_3 (.a(R), .b({32{1'b0}}), .eq(Flags[2]));  // open: gt, lt
  BitSelector #(.width(32)) bitselector_21 (.in(R), .out(Flags[3]), .sel({5{1'b1}}));
  Multiplexer #(.select(4)) multiplexer_1 (
    .in0(1'b0), .in1(1'b0), .in2(CoutLSL), .in3(CoutLSR), .in4(CoutASR), .in5(CoutADC), .in6(CoutSBC),
    .in7(CoutROR), .in8(1'b0), .in9(1'b0), .in10(CoutCMP), .in11(CoutCMN), .in12(1'b0), .in13(1'b0),
    .in14(1'b0), .in15(1'b0), .out(Flags[1]), .sel(Codop));
  Multiplexer #(.select(4)) multiplexer_2 (
    .in0(1'b0), .in1(1'b0), .in2(1'b0), .in3(1'b0), .in4(1'b0), .in5(VADC), .in6(VSBC), .in7(1'b0),
    .in8(1'b0), .in9(VRSD), .in10(VCMP), .in11(VCMN), .in12(1'b0), .in13(1'b0), .in14(1'b0), .in15(1'b0),
    .out(Flags[0]), .sel(Codop));
  Multiplexer #(.select(4), .width(32)) multiplexer_3 (
    .in0(R), .in1(R), .in2(R), .in3(R), .in4(R), .in5(R), .in6(R), .in7(R), .in8(R), .in9(R), .in10(B),
    .in11(B), .in12(R), .in13(R), .in14(R), .in15(R), .out(S), .sel(Codop));

  // Other names for the same wires on the sheet: C = CarryIn; Cod[3:0] = Codop; V = Flags[0]; Cout = Flags[1];
  //   Z = Flags[2]; N = Flags[3]; S_t[4:0] = Shift

  // Notes on the sheet:
  //   Note: for ROR, C = N
  //   Note 2: assume that shift > 0 for LSL and LSR
  //   check
  //   check
  //   check
  //   check
  //   check
endmodule
