// Logisim project BancDeRegistres.circ as structural Verilog: 1 circuit, main circuit BancRegistre
module BancRegistre (
  input  [31:0] DataIn,
  input  [2:0] RegA,
  input  [2:0] RegDest,
  input  [2:0] RegB,
  input  Clk,
  input  Reset,
  output [31:0] R0Debug,
  output [31:0] R1Debug,
  output [31:0] AOut,
  output [31:0] R2Debug,
  output [31:0] R3Debug,
  output [31:0] R4Debug,
  output [31:0] R5Debug,
  output [31:0] BOut,
  output [31:0] R6Debug,
  output [31:0] R7Debug
);

  wire decoder_1_out0, decoder_1_out1, decoder_1_out2, decoder_1_out3, decoder_1_out4, decoder_1_out5,
       decoder_1_out6, decoder_1_out7;

  Decoder #(.enable("false"), .select(3)) decoder_1 (
    .out0(decoder_1_out0), .out1(decoder_1_out1), .out2(decoder_1_out2), .out3(decoder_1_out3),
    .out4(decoder_1_out4), .out5(decoder_1_out5), .out6(decoder_1_out6), .out7(decoder_1_out7), .sel(RegDest));
  Register #(.width(32)) R0 (.D(DataIn), .en(decoder_1_out0), .clk(Clk), .Q(R0Debug), .clr(Reset));
  Register #(.width(32)) R1 (.D(DataIn), .en(decoder_1_out1), .clk(Clk), .Q(R1Debug), .clr(Reset));
  Register #(.width(32)) R2 (.D(DataIn), .en(decoder_1_out2), .clk(Clk), .Q(R2Debug), .clr(Reset));
  Register #(.width(32)) R3 (.D(DataIn), .en(decoder_1_out3), .clk(Clk), .Q(R3Debug), .clr(Reset));
  Register #(.width(32)) R4 (.D(DataIn), .en(decoder_1_out4), .clk(Clk), .Q(R4Debug), .clr(Reset));
  Register #(.width(32)) R5 (.D(DataIn), .en(decoder_1_out5), .clk(Clk), .Q(R5Debug), .clr(Reset));
  Register #(.width(32)) R6 (.D(DataIn), .en(decoder_1_out6), .clk(Clk), .Q(R6Debug), .clr(Reset));
  Register #(.width(32)) R7 (.D(DataIn), .en(decoder_1_out7), .clk(Clk), .Q(R7Debug), .clr(Reset));
  Multiplexer #(.select(3), .width(32)) multiplexer_1 (
    .in0(R0Debug), .in1(R1Debug), .in2(R2Debug), .in3(R3Debug), .in4(R4Debug), .in5(R5Debug), .in6(R6Debug),
    .in7(R7Debug), .out(AOut), .sel(RegA));
  Multiplexer #(.select(3), .width(32)) multiplexer_2 (
    .in0(R0Debug), .in1(R1Debug), .in2(R2Debug), .in3(R3Debug), .in4(R4Debug), .in5(R5Debug), .in6(R6Debug),
    .in7(R7Debug), .out(BOut), .sel(RegB));

  // Other names for the same wires on the sheet: R0E[31:0] = R0Debug; R1E[31:0] = R1Debug; R2E[31:0] = R2Debug;
  //   R3E[31:0] = R3Debug; R4E[31:0] = R4Debug; R5E[31:0] = R5Debug; R6E[31:0] = R6Debug; R7E[31:0] = R7Debug
endmodule
