// Logisim project Ctl_Data_Processing.circ as structural Verilog: 2 circuits, main circuit Data_Processing
module Data_Processing (
  input  [15:0] Instruction,
  input  Enable,
  output [2:0] Rd,
  output [2:0] Rn,
  output [2:0] Rm,
  output [3:0] ALU_Opcode,
  output [3:0] Flags_Update_Mask
);

  wire [15:10] multiplexer_1_out;

  Multiplexer #(.width(16)) multiplexer_1 (
    .in0({16{1'b0}}), .in1(Instruction), .out({multiplexer_1_out, ALU_Opcode, Rm, Rd}), .sel(Enable));
  FlagUpdater flagupdater_1 (
    .c0(ALU_Opcode[3]), .c1(ALU_Opcode[2]), .c2(ALU_Opcode[1]), .c3(ALU_Opcode[0]), .enable(Enable),
    .v(Flags_Update_Mask[0]), .c(Flags_Update_Mask[1]), .z(Flags_Update_Mask[2]), .n(Flags_Update_Mask[3]));

  assign Rn = Rd;

  // Notes on the sheet:
  //   Note 2: RSB instruction has Rn as 1st operand.
  //   Pull output low on Enable = 0
  //   MUL instruction has Rn as 1st operand and Rdm as 2nd operand
  //   For simplification purposes, Rm is used for 1st operand both here and in the ALU.
  //   Note: instructions that does not save the result will still have the second operand as the destination register, the ALU will copy the second register to the destination register
endmodule

module FlagUpdater (
  input  c0,
  input  c1,
  input  c2,
  input  c3,
  input  enable,
  output v,
  output c,
  output z,
  output n
);

  wire and_1_out, and_2_out, and_3_out, and_4_out, and_5_out, and_6_out, and_7_out, not_1_out, not_2_out,
       not_3_out, not_4_out, or_1_out, or_2_out;

  not not_1 (not_1_out, c0);
  not not_2 (not_2_out, c1);
  not not_3 (not_3_out, c2);
  not not_4 (not_4_out, c3);
  and and_1 (and_1_out, not_1_out, c1, not_3_out, c3);
  and and_2 (and_2_out, not_1_out, c1, c2, not_4_out);
  and and_3 (and_3_out, c0, not_2_out, c3);
  and and_4 (and_4_out, c0, not_2_out, c2);
  and and_5 (and_5_out, not_1_out, c1);
  and and_6 (and_6_out, c0, not_2_out, c3);
  and and_7 (and_7_out, not_2_out, c2);
  or or_1 (or_1_out, and_1_out, and_2_out, and_3_out, and_4_out);
  or or_2 (or_2_out, and_5_out, and_6_out, and_7_out);
  and and_8 (c, or_2_out, enable);
  and and_9 (v, or_1_out, enable);

  assign n = enable;
  assign z = enable;
endmodule
