// Logisim project Ctl_Shift_Add_Sub_Mov.circ as structural Verilog: 3 circuits, main circuit Shift_Add_Sub_Mov
module Shift_Add_Sub_Mov (
  input  [15:0] Instruction,
  input  Enable,
  output [3:0] Flags_Update_Mask,
  output [3:0] ALU_Opcode,
  output [2:0] Rd,
  output [4:0] Imm5,
  output [31:0] Imm32,
  output Imm32_Enable,
  output [2:0] Rm,
  output [2:0] Rn,
  output Carry
);

  wire and_1_out, and_2_out, and_3_out, and_7_out, decoder_1_out0, decoder_1_out1, decoder_1_out2,
       decoder_1_out3, decoder_1_out4, decoder_1_out5, decoder_1_out6, decoder_1_out7, decoder_2_out0,
       decoder_2_out1, decoder_2_out2, decoder_2_out3, or_1_out, or_2_out, or_3_out, or_4_out, or_5_out,
       or_6_out, or_7_out, or_8_out;
  wire [2:0] bit_extender_9_out, or_11_out, or_12_out, or_13_out;
  wire [3:0] flagsupdate_1_sortie, opcode_1_sortie;
  wire [4:0] bit_extender_8_out;
  wire [7:0] or_10_out;
  wire [15:0] and_4_out, and_5_out, and_6_out, and_8_out, and_9_out, bit_extender_1_out, bit_extender_2_out,
       bit_extender_3_out, bit_extender_4_out, bit_extender_5_out;
  wire [31:0] bit_extender_6_out, bit_extender_7_out, bit_extender_10_out, multiplexer_3_out, negator_1_out,
       or_14_out;

  Decoder #(.select(3)) decoder_1 (
    .out0(decoder_1_out0), .out1(decoder_1_out1), .out2(decoder_1_out2), .out3(decoder_1_out3),
    .out4(decoder_1_out4), .out5(decoder_1_out5), .out6(decoder_1_out6), .out7(decoder_1_out7),
    .sel(Instruction[13:11]));  // open: en
  Decoder #(.select(2)) decoder_2 (
    .out0(decoder_2_out0), .out1(decoder_2_out1), .out2(decoder_2_out2), .out3(decoder_2_out3),
    .sel(Instruction[10:9]));  // open: en
  FlagsUpdate flagsupdate_1 (.entree(Instruction[13:11]), .sortie(flagsupdate_1_sortie));
  Opcode opcode_1 (.entree(Instruction[13:9]), .sortie(opcode_1_sortie));
  Multiplexer #(.width(4)) multiplexer_1 (
    .in0(4'b0000), .in1(flagsupdate_1_sortie), .out(Flags_Update_Mask), .sel(Enable));
  Multiplexer #(.width(4)) multiplexer_2 (.in0(4'b0000), .in1(opcode_1_sortie), .out(ALU_Opcode), .sel(Enable));
  or or_1 (or_1_out, decoder_1_out0, decoder_1_out1, decoder_1_out2);
  or or_2 (or_2_out, decoder_1_out4, decoder_1_out5);
  or or_3 (or_3_out, decoder_1_out6, decoder_1_out7);
  or or_4 (or_4_out, decoder_2_out2, decoder_2_out3);
  or or_5 (or_5_out, decoder_2_out0, decoder_2_out1);
  or or_6 (or_6_out, decoder_2_out2, decoder_2_out3);
  or or_7 (or_7_out, decoder_2_out3, decoder_2_out1);
  assign bit_extender_1_out = {{15{or_1_out}}, or_1_out};  // Bit_Extender bit_extender_1
  assign bit_extender_2_out = {{15{or_2_out}}, or_2_out};  // Bit_Extender bit_extender_2
  assign bit_extender_3_out = {{15{or_3_out}}, or_3_out};  // Bit_Extender bit_extender_3
  and and_1 (and_1_out, decoder_1_out3, or_4_out);
  and and_2 (and_2_out, decoder_1_out3, or_5_out);
  and and_3 (and_3_out, decoder_1_out3, or_6_out);
  assign and_4_out = bit_extender_1_out & Instruction;  // AND_Gate and_4, 16 bits wide
  assign and_5_out = bit_extender_2_out & Instruction;  // AND_Gate and_5, 16 bits wide
  assign and_6_out = bit_extender_3_out & Instruction;  // AND_Gate and_6, 16 bits wide
  assign bit_extender_4_out = {{15{and_2_out}}, and_2_out};  // Bit_Extender bit_extender_4
  assign bit_extender_5_out = {{15{and_3_out}}, and_3_out};  // Bit_Extender bit_extender_5
  and and_7 (and_7_out, or_7_out, decoder_1_out3);
  or or_8 (or_8_out, and_1_out, decoder_1_out4, decoder_1_out5, decoder_1_out6, decoder_1_out7);
  assign and_8_out = bit_extender_4_out & Instruction;  // AND_Gate and_8, 16 bits wide
  assign and_9_out = bit_extender_5_out & Instruction;  // AND_Gate and_9, 16 bits wide
  or or_9 (Carry, and_7_out, decoder_1_out7);
  assign or_10_out = and_5_out[7:0] | and_6_out[7:0];  // OR_Gate or_10, 8 bits wide
  assign bit_extender_6_out = {{24{1'b0}}, or_10_out};  // Bit_Extender bit_extender_6
  assign or_11_out = and_4_out[2:0] | and_8_out[2:0] | and_9_out[2:0] | and_5_out[10:8] | and_6_out[10:8];  // OR_Gate or_11, 3 bits wide
  assign bit_extender_7_out = {{29{1'b0}}, and_9_out[8:6]};  // Bit_Extender bit_extender_7
  Negator #(.width(32)) negator_1 (.in(bit_extender_6_out), .out(negator_1_out));
  assign or_12_out = and_8_out[5:3] | and_9_out[5:3] | and_4_out[5:3] | and_6_out[10:8];  // OR_Gate or_12, 3 bits wide
  assign bit_extender_8_out = {{4{Enable}}, Enable};  // Bit_Extender bit_extender_8
  Multiplexer #(.width(32)) multiplexer_3 (
    .in0(bit_extender_6_out), .in1(negator_1_out), .out(multiplexer_3_out), .sel(decoder_1_out4));
  assign or_13_out = and_4_out[5:3] | and_8_out[8:6];  // OR_Gate or_13, 3 bits wide
  assign bit_extender_9_out = {{2{Enable}}, Enable};  // Bit_Extender bit_extender_9
  assign Rd = or_11_out & bit_extender_9_out;  // AND_Gate and_10, 3 bits wide
  assign Imm5 = and_4_out[10:6] & bit_extender_8_out;  // AND_Gate and_11, 5 bits wide
  assign or_14_out = bit_extender_7_out | multiplexer_3_out;  // OR_Gate or_14, 32 bits wide
  assign bit_extender_10_out = {{31{Enable}}, Enable};  // Bit_Extender bit_extender_10
  and and_12 (Imm32_Enable, Enable, or_8_out);
  assign Rm = bit_extender_9_out & or_13_out;  // AND_Gate and_13, 3 bits wide
  assign Rn = bit_extender_9_out & or_12_out;  // AND_Gate and_14, 3 bits wide
  assign Imm32 = or_14_out & bit_extender_10_out;  // AND_Gate and_15, 32 bits wide

  // Notes on the sheet:
  //   Pull output low on Enable = 0
  //   Note 3: Imm32_Enable forces the use of the immediate for Rm register
  //   Note: ALU uses Rn register for shifts. Use Rn instead of Rm for shifts (immediate) here too
  //   Note 2: MOV uses RSB ALU opcode with Imm8 reversed so that it is copied to output register
  //   only ADD and SUB use Rm
  //   ALU will use Imm32 instead of Rm
  //   Enable carry for SUB since it is reversed in ALU
endmodule

module Opcode (
  input  [4:0] entree,
  output [3:0] sortie
);

  wire and_2_out, and_3_out, and_4_out, and_5_out, and_6_out, and_7_out, not_1_out, not_2_out, not_3_out,
       not_4_out;

  not not_1 (not_1_out, entree[4]);
  not not_2 (not_2_out, entree[3]);
  not not_3 (not_3_out, entree[2]);
  not not_4 (not_4_out, entree[0]);
  and and_1 (sortie[3], entree[4], not_2_out);
  and and_2 (and_2_out, not_1_out, not_2_out);
  and and_3 (and_3_out, entree[2], entree[0]);
  or or_1 (sortie[1], and_2_out, and_3_out, and_4_out);
  and and_4 (and_4_out, entree[4], entree[2]);
  and and_5 (and_5_out, not_1_out, not_2_out, entree[2]);
  and and_6 (and_6_out, not_1_out, entree[2], not_4_out);
  or or_2 (sortie[0], and_5_out, and_6_out, and_7_out);
  and and_7 (and_7_out, entree[4], not_3_out);

  assign sortie[2] = entree[3];
endmodule

module FlagsUpdate (
  input  [2:0] entree,
  output [3:0] sortie
);

  wire and_1_out, and_2_out, and_3_out, not_1_out;

  not not_1 (not_1_out, entree[2]);
  or or_1 (sortie[1], not_1_out, entree[0], entree[1]);
  and and_1 (and_1_out, entree[1], entree[0]);
  and and_2 (and_2_out, entree[2], entree[0]);
  and and_3 (and_3_out, entree[2], entree[1]);
  or or_2 (sortie[0], and_1_out, and_2_out, and_3_out);

  assign sortie[3:2] = 2'b11;
endmodule
